// Logisim project 3x3.circ as structural Verilog: 4 circuits, main circuit main
module main (
  input  [2:0] x,
  input  [2:0] y,
  input  kb0,
  input  sub_add,
  output [2:0] D_S,
  output B_C,
  output L,
  output subOverflow,
  output addOverflow
);

  wire and_1_out, and_2_out, and_3_out, and_4_out;
  wire [2:0] G_out, P_out, Q_out, xor_1_out;
  wire [2:1] kb1_1_kb1;

  assign xor_1_out = {3{sub_add}} ^ x;  // XOR_Gate xor_1, 3 bits wide
  assign G_out = xor_1_out & y;  // AND_Gate G, 3 bits wide
  assign P_out = xor_1_out | y;  // OR_Gate P, 3 bits wide
  assign Q_out = x ^ y;  // XOR_Gate Q, 3 bits wide
  kb1 kb1_1 (.P(P_out), .G(G_out), .kb0(kb0), .kb1(kb1_1_kb1[1]));
  kb2 kb2_1 (.P(P_out), .G(G_out), .kb0(kb0), .kb2(kb1_1_kb1[2]));
  kb3 kb3_1 (.P(P_out), .G(G_out), .kb0(kb0), .kb3(B_C));
  assign D_S = {kb1_1_kb1, kb0} ^ Q_out;  // XOR_Gate S, 3 bits wide
  and and_1 (and_1_out, ~x[2], y[2], D_S[2]);  // AND_Gate
  and and_2 (and_2_out, x[2], ~y[2], ~D_S[2]);  // AND_Gate
  and and_3 (and_3_out, ~x[2], ~x[2], D_S[2]);  // AND_Gate
  and and_4 (and_4_out, x[2], y[2], ~D_S[2]);  // AND_Gate
  or or_1 (subOverflow, and_1_out, and_2_out);
  or or_2 (addOverflow, and_3_out, and_4_out);
  xor xor_2 (L, D_S[2], subOverflow);

  // Other names for the same wires on the sheet: dss = D_S[2]; xs = x[2]; ys = y[2]
endmodule

module kb1 (
  input  [2:0] P,
  input  [2:0] G,
  input  kb0,
  output kb1
);

  wire p0kb0_out;

  and p0kb0 (p0kb0_out, P[0], kb0);
  or or_1 (kb1, p0kb0_out, G[0]);
endmodule

module kb2 (
  input  [2:0] P,
  input  [2:0] G,
  input  kb0,
  output kb2
);

  wire p1g0_out, p1p0kb0_out;

  and p1p0kb0 (p1p0kb0_out, P[0], P[1], kb0);
  and p1g0 (p1g0_out, P[1], G[0]);
  or or_1 (kb2, p1g0_out, p1p0kb0_out, G[1]);
endmodule

module kb3 (
  input  [2:0] P,
  input  [2:0] G,
  input  kb0,
  output kb3
);

  wire and_1_out, and_2_out, and_3_out;

  and and_1 (and_1_out, P[0], P[1], P[2], kb0);
  and and_2 (and_2_out, P[1], P[2], G[0]);
  and and_3 (and_3_out, P[2], G[1]);
  or or_1 (kb3, and_1_out, and_2_out, and_3_out, G[2]);
endmodule
