// Logisim project processor0003.circ as structural Verilog: 1 circuit, main circuit main
module main (
  output [7:0] regA,
  output [7:0] regB,
  output [7:0] regC,
  output [7:0] regD,
  output [4:0] flags,
  output [7:0] D,
  output RAMSel,
  output RAMLd,
  output [7:0] A,
  output [7:0] PC,
  output RAMClk,
  output opFetch,
  output halt
);

  wire AddrMux, ALUen, and_1_out, button_2_out, clk, FC, not_1_out, or_1_out, or_2_out, PCEn, PCInc, PCMux,
       reset, RIEn, RIMux, RO0En, RO1DMX;
  wire [1:0] RISel, RO0DMX, RO0Sel, RO1Sel;
  wire [2:0] ALUop, PCMuxMux;
  wire [4:0] alu_1_p6;
  wire [7:0] adder_1_out, alu_1_p5, demultiplexer_1_out0, demultiplexer_1_out1, demultiplexer_2_out0,
       demultiplexer_2_out1, instruction, multiplexer_1_out, multiplexer_2_out, multiplexer_3_out,
       multiplexer_5_out, regbank_1_regout0, regbank_1_regout1;
  wire [11:0] adder_2_out, multiplexer_4_out, ucodePtr_q;
  wire [25:24] rom_1_data;

  Clock clock_1 (.out(clk));
  and and_1 (and_1_out, PCMux, ~RO0En);  // AND_Gate
  Multiplexer #(.width(8), .enable("false")) multiplexer_1 (
    .in0(demultiplexer_1_out0), .in1(D), .out(multiplexer_1_out), .sel(and_1_out));
  Button button_1 (.out(reset));
  Multiplexer #(.width(8)) multiplexer_2 (.in0(D), .in1(alu_1_p5), .out(multiplexer_2_out), .sel(RIMux), .en(RIEn));
  Multiplexer #(.width(8), .enable("false")) multiplexer_3 (
    .in0(adder_1_out), .in1(multiplexer_1_out), .out(multiplexer_3_out), .sel(PCMux));
  regBank regbank_1 (
    .regInSel(RISel), .regOut0(regbank_1_regout0), .RegOut0Sel(RO0Sel), .regOut1(regbank_1_regout1),
    .regOut1Sel(RO1Sel), .clk(clk), .reset(reset), .regIn(multiplexer_2_out), .inEn(RIEn), .A(regA),
    .B(regB), .C(regC), .D(regD));
  or or_1 (or_1_out, PCInc, AddrMux);
  Register u_PC (.D(multiplexer_3_out), .en(PCEn), .Q(PC), .clk(clk), .clr(reset));
  Adder adder_1 (.a(PC), .b({8{1'b0}}), .out(adder_1_out), .cin(or_1_out));  // open: cout
  Demultiplexer #(.select(2), .width(8)) demultiplexer_1 (
    .out0(demultiplexer_1_out0), .out1(demultiplexer_1_out1), .out2(D), .in(regbank_1_regout0), .sel(RO0DMX),
    .en(RO0En));  // open: out3
  Demultiplexer #(.width(8), .enable("false")) demultiplexer_2 (
    .out0(demultiplexer_2_out0), .out1(demultiplexer_2_out1), .in(regbank_1_regout1), .sel(RO1DMX));
  Multiplexer #(.width(12), .enable("false")) multiplexer_4 (
    .in0({instruction, 4'b0000}), .in1(adder_2_out), .out(multiplexer_4_out), .sel(rom_1_data[24]));
  nand nand_1 (FC, RO1DMX, ALUen);
  Multiplexer #(.width(8), .enable("false")) multiplexer_5 (
    .in0(demultiplexer_2_out1), .in1(8'h1), .out(multiplexer_5_out), .sel(FC));
  not not_1 (not_1_out, FC);
  Register InstructionReg (.D(D), .en(opFetch), .Q(instruction), .clk(clk), .clr(reset));
  Register #(.width(12), .trigger("falling")) ucodePtr (
    .D(multiplexer_4_out), .en(1'b1), .Q(ucodePtr_q), .clk(clk), .clr(or_2_out));
  // ALU alu_1: pin names not known; wires that end beside it: demultiplexer_1_out1, multiplexer_5_out, ALUen, ALUop, alu_1_p5, alu_1_p6, flags
  Register #(.width(5)) u_flags (.D(alu_1_p6), .en(not_1_out), .Q(flags), .clk(clk), .clr(reset));
  Adder #(.width(12)) adder_2 (.a(ucodePtr_q), .b({12{1'b0}}), .out(adder_2_out), .cin(1'b1));  // open: cout
  Multiplexer #(.width(8), .enable("false")) multiplexer_6 (
    .in0(demultiplexer_2_out0), .in1(PC), .out(A), .sel(AddrMux));
  or or_2 (or_2_out, rom_1_data[25], reset);
  Multiplexer #(.select(3), .enable("false")) multiplexer_7 (
    .in0(flags[0]), .in1(flags[1]), .in2(flags[2]), .in3(flags[3]), .in4(flags[4]), .in5(1'b0), .in6(1'b0),
    .in7(1'b1), .out(PCMux), .sel(PCMuxMux));
  ROM #(.addrWidth(12), .dataWidth(26)) rom_1 (
    .addr(ucodePtr_q),
    .data({rom_1_data, PCEn, PCMuxMux, AddrMux, ALUop, ALUen, RO1DMX, RO1Sel, RO0DMX, RO0Sel, RO0En, RISel, RIEn, RIMux, RAMLd, RAMSel, opFetch}),
    .sel(1'b1));
  Multiplexer #(.select(3), .enable("false")) multiplexer_8 (
    .in0(PCMux), .in1(PCMux), .in2(PCMux), .in3(PCMux), .in4(PCMux), .in5(1'b1), .in6(1'b1), .in7(1'b1),
    .out(PCInc), .sel(PCMuxMux));
  Comparator #(.width(26)) comparator_1 (
    .a({rom_1_data, PCEn, PCMuxMux, AddrMux, ALUop, ALUen, RO1DMX, RO1Sel, RO0DMX, RO0Sel, RO0En, RISel, RIEn, RIMux, RAMLd, RAMSel, opFetch}),
    .b({26{1'b0}}), .eq(halt));  // open: gt, lt
  Button button_2 (.out(button_2_out));
  RAM ram_1 (.addr(A), .data(D), .sel(RAMSel), .clk(clk), .ld(RAMLd), .clr(button_2_out));
  and and_2 (RAMClk, RAMSel, ~RAMLd, clk);  // AND_Gate

  // Other names for the same wires on the sheet: ucodeData[20:0] = {PCEn, PCMuxMux, AddrMux, ALUop, ALUen, RO1DMX, RO1Sel, RO0DMX, RO0Sel, RO0En, RISel, RIEn, RIMux}

  // Notes on the sheet:
  //   contents of rom_1 (hex, n*v repeats v):
  //   1080007 d80004 1022*0 1f80006 2000000 14*0 1c80006 2000000 14*0 1b80006 2000000 14*0 1a80006 2000000
  //   14*0 1880006 2000000 14*0 1980006 2000000 174*0 1500890 2000000 14*0 1500990 2000000 14*0 1500a90
  //   2000000 14*0 1500b90 2000000 14*0 15008b0 2000000 14*0 15009b0 2000000 14*0 1500ab0 2000000 14*0
  //   1500bb0 2000000 14*0 15008d0 2000000 14*0 15009d0 2000000 14*0 1500ad0 2000000 14*0 1500bd0 2000000
  //   14*0 15008f0 2000000 14*0 15009f0 2000000 14*0 1500af0 2000000 14*0 1500bf0 2000000 14*0 1c00080
  //   2000000 14*0 1c00180 2000000 14*0 1c00280 2000000 14*0 1c00380 2000000 14*0 1b00080 2000000 14*0
  //   1b00180 2000000 14*0 1b00280 2000000 14*0 1b00380 2000000 14*0 1a00080 2000000 14*0 1a00180 2000000
  //   14*0 1a00280 2000000 14*0 1a00380 2000000 14*0 1d80016 2000000 14*0 1d80036 2000000 14*0 1d80056
  //   2000000 14*0 1d80076 2000000 14*0 1500016 2000000 14*0 1501016 2000000 14*0 1502016 2000000 14*0
  //   1503016 2000000 14*0 1500036 2000000 14*0 1501036 2000000 14*0 1502036 2000000 14*0 1503036 2000000
  //   14*0 1500056 2000000 14*0 1501056 2000000 14*0 1502056 2000000 14*0 1503056 2000000 14*0 1500076
  //   2000000 14*0 1501076 2000000 14*0 1502076 2000000 14*0 1503076 2000000 14*0 150c498 2000000 14*0
  //   150d498 2000000 14*0 150e498 2000000 14*0 150f498 2000000 14*0 150c5b8 2000000 14*0 150d5b8 2000000
  //   14*0 150e5b8 2000000 14*0 150f5b8 2000000 14*0 150c6d8 2000000 14*0 150d6d8 2000000 14*0 150e6d8
  //   2000000 14*0 150f6d8 2000000 14*0 150c7f8 2000000 14*0 150d7f8 2000000 14*0 150e7f8 2000000 14*0
  //   150f7f8 2000000 14*0 151c498 2000000 14*0 151d498 2000000 14*0 151e498 2000000 14*0 151f498 2000000
  //   14*0 151c5b8 2000000 14*0 151d5b8 2000000 14*0 151e5b8 2000000 14*0 151f5b8 2000000 14*0 151c6d8
  //   2000000 14*0 151d6d8 2000000 14*0 151e6d8 2000000 14*0 151f6d8 2000000 14*0 151c7f8 2000000 14*0
  //   151d7f8 2000000 14*0 151e7f8 2000000 14*0 151f7f8 2000000 14*0 152c498 2000000 14*0 152d498 2000000
  //   14*0 152e498 2000000 14*0 152f498 2000000 14*0 152c5b8 2000000 14*0 152d5b8 2000000 14*0 152e5b8
  //   2000000 14*0 152f5b8 2000000 14*0 152c6d8 2000000 14*0 152d6d8 2000000 14*0 152e6d8 2000000 14*0
  //   152f6d8 2000000 14*0 152c7f8 2000000 14*0 152d7f8 2000000 14*0 152e7f8 2000000 14*0 152f7f8 2000000
  //   14*0 1538498 2000000 14*0 1f00080 2000000 14*0 1800080 2000000 14*0 1900080 2000000 14*0 15385b8
  //   2000000 14*0 1f00180 2000000 14*0 1800180 2000000 14*0 1900180 2000000 14*0 15386d8 2000000 14*0
  //   1f00280 2000000 14*0 1800280 2000000 14*0 1900280 2000000 14*0 15387f8 2000000 14*0 1f00380 2000000
  //   14*0 1800380 2000000 14*0 1900380 2000000 14*0 154c498 2000000 14*0 154d498 2000000 14*0 154e498
  //   2000000 14*0 154f498 2000000 14*0 154c5b8 2000000 14*0 154d5b8 2000000 14*0 154e5b8 2000000 14*0
  //   154f5b8 2000000 14*0 154c6d8 2000000 14*0 154d6d8 2000000 14*0 154e6d8 2000000 14*0 154f6d8 2000000
  //   14*0 154c7f8 2000000 14*0 154d7f8 2000000 14*0 154e7f8 2000000 14*0 154f7f8 2000000 14*0 1508498
  //   2000000 14*0 155d498 2000000 14*0 155e498 2000000 14*0 155f498 2000000 14*0 155c5b8 2000000 14*0
  //   15085b8 2000000 14*0 155e5b8 2000000 14*0 155f5b8 2000000 14*0 155c6d8 2000000 14*0 155d6d8 2000000
  //   14*0 15086d8 2000000 14*0 155f6d8 2000000 14*0 155c7f8 2000000 14*0 155d7f8 2000000 14*0 155e7f8
  //   2000000 14*0 15087f8 2000000 14*0 1518498 2000000 14*0 151d488 2000000 14*0 151e488 2000000 14*0
  //   151f488 2000000 14*0 151c5a8 2000000 14*0 15185b8 2000000 14*0 151e5a8 2000000 14*0 151f5a8 2000000
  //   14*0 151c6c8 2000000 14*0 151d6c8 2000000 14*0 15186d8 2000000 14*0 151f6c8 2000000 14*0 151c7e8
  //   2000000 14*0 151d7e8 2000000 14*0 151e7e8 2000000 14*0 15187f8 2000000 14*0 1500882 2000000 14*0
  //   1501882 2000000 14*0 1502882 2000000 14*0 1503882 2000000 14*0 1500982 2000000 14*0 1501982 2000000
  //   14*0 1502982 2000000 14*0 1503982 2000000 14*0 1500a82 2000000 14*0 1501a82 2000000 14*0 1502a82
  //   2000000 14*0 1503a82 2000000 14*0 1500b82 2000000 14*0 1501b82 2000000 14*0 1502b82 2000000 14*0
  //   1503b82 2000000
endmodule
