// Logisim project regbank.circ as structural Verilog: 1 circuit, main circuit regBank
module regBank (
  input  [7:0] regIn,
  input  inEn,
  input  [1:0] RegOut0Sel,
  input  [1:0] regInSel,
  input  [1:0] regOut1Sel,
  input  clk,
  input  reset,
  output [7:0] A,
  output [7:0] B,
  output [7:0] C,
  output [7:0] D,
  output [7:0] regOut0,
  output [7:0] regOut1
);

  wire decoder_1_out0, decoder_1_out1, decoder_1_out2, decoder_1_out3;

  Decoder #(.select(2), .disabled(0)) decoder_1 (
    .out0(decoder_1_out0), .out1(decoder_1_out1), .out2(decoder_1_out2), .out3(decoder_1_out3),
    .sel(regInSel), .en(inEn));
  Register u_A (.D(regIn), .en(decoder_1_out0), .Q(A), .clk(clk), .clr(reset));
  Register u_B (.D(regIn), .en(decoder_1_out1), .Q(B), .clk(clk), .clr(reset));
  Register u_C (.D(regIn), .en(decoder_1_out2), .Q(C), .clk(clk), .clr(reset));
  Register u_D (.D(regIn), .en(decoder_1_out3), .Q(D), .clk(clk), .clr(reset));
  Multiplexer #(.select(2), .width(8), .enable("false")) multiplexer_1 (
    .in0(A), .in1(B), .in2(C), .in3(D), .out(regOut0), .sel(RegOut0Sel));
  Multiplexer #(.select(2), .width(8), .enable("false")) multiplexer_2 (
    .in0(A), .in1(B), .in2(C), .in3(D), .out(regOut1), .sel(regOut1Sel));
endmodule
