// Logisim project 3x3adder.circ as structural Verilog: 4 circuits, main circuit main
module main (
  input  [2:0] X,
  input  [2:0] Y,
  input  k,
  output k3,
  output [2:0] S
);

  wire [2:0] G, P, Q;
  wire [2:1] k1_1_k1;

  assign P = X | Y;  // OR_Gate or_1, 3 bits wide
  assign G = X & Y;  // AND_Gate and_1, 3 bits wide
  assign Q = X ^ Y;  // XOR_Gate xor_1, 3 bits wide
  k3 k3_1 (.G(G), .P(P), .k0(k), .k3(k3));
  k2 k2_1 (.G(G), .P(P), .k0(k), .k2(k1_1_k1[2]));
  k1 k1_1 (.G(G), .P(P), .k0(k), .k1(k1_1_k1[1]));
  assign S = Q ^ {k1_1_k1, k};  // XOR_Gate xor_2, 3 bits wide

  // Other names for the same wires on the sheet: k0 = k
endmodule

module k1 (
  input  [2:0] G,
  input  [2:0] P,
  input  k0,
  output k1
);

  wire and_1_out;

  and and_1 (and_1_out, P[0], k0);
  or or_1 (k1, G[0], and_1_out);
endmodule

module k2 (
  input  [2:0] G,
  input  [2:0] P,
  input  k0,
  output k2
);

  wire and_1_out, and_2_out;

  and and_1 (and_1_out, G[0], P[1]);
  and and_2 (and_2_out, P[0], P[1], k0);
  or or_1 (k2, and_1_out, G[1], and_2_out);
endmodule

module k3 (
  input  [2:0] G,
  input  [2:0] P,
  input  k0,
  output k3
);

  wire and_1_out, and_2_out, and_3_out;

  and and_1 (and_1_out, G[1], P[2]);
  and and_2 (and_2_out, P[1], P[2], G[0]);
  and and_3 (and_3_out, P[0], P[2], P[1], k0);
  or or_1 (k3, G[2], and_1_out, and_2_out, and_3_out);
endmodule
