// Logisim project multi.circ as structural Verilog: 1 circuit, main circuit main
module main (
  input  [3:0] X,
  input  [3:0] Y,
  output out_3,
  output out_4,
  output [3:0] out_5
);

  assign {out_5[3], out_4, out_3, out_5[0]} = X & Y;  // AND_Gate and_1, 4 bits wide

  assign out_5[2:1] = {out_4, out_3};
endmodule
